# Fritzing sketch OpenPull (saved by Fritzing 0.9.4)
perfboards: 1
breadboards: 1

parts:
  R5 = Resistor [tolerance=±5% resistance=1k package=THT]
  S1 = Pushbutton [package="[THT]"]
  R4 = Resistor [tolerance=±5% resistance=1k package=THT]
  FAN = Fan - Ventilador [package=THT]
  Bauteil4 = Arduino Micro (Rev3)
  U1 = Mini-360 DC-DC Buck converter [package=THT]
  S4 = Pushbutton [package="[THT]"]
  C1 = Electrolytic Capacitor [capacitance=0.1mF voltage=35V package="100 mil [THT, electrolytic]"]
  R2 = Resistor [tolerance=±5% resistance=1k package=THT]
  J1 = female pin header, 4 pins [form="♀ (female)"]
  Power_plug1 = Power plug
  S5 = Toggle Switch [package=THT]
  Part1 = HX711 Weighing Sensor Module
  M2 = Stepper Motor - Bipolar
  R3 = Resistor [tolerance=±5% resistance=1k package=THT]
  LED1 = LED - 5mm [color="Green (555nm)" package="5 mm [THT]"]
  M1 = Stepper Motor - Bipolar
  R6 = Resistor [tolerance=±5% resistance=220 package=THT]
  SdDetectPin = Header 1 [package=1x01_offset]
  Pololu_A3 = Pololu A4988 [package=SO16]
  Pololu_A4 = Pololu A4988 [package=SO16]
  HM10_Ble_Module = Bluetooth HM-10
  microSD1 = MicroSD Card Module

nets:
  N1: R5.Pin_0, R4.Pin_1, Part1.E+
  N2: R5.Pin_1, R2.Pin_1, Part1.A-
  N3: S1.Pin_1, S1.Pin_2, Bauteil4.D4_PWM/A6, J1.pin3
  GND: S1.Pin_3, S1.Pin_4, Bauteil4.GND, U1.OUT-, S4.Pin_3, S4.Pin_4, J1.pin4, S5.COM, Part1.GND, R6.Pin_0, Pololu_A3.MS2, Pololu_A3.MS3, Pololu_A3.GND#8, Pololu_A4.MS2, Pololu_A4.MS3, Pololu_A4.GND#8, HM10_Ble_Module.GND, HM10_Ble_Module.STATE, HM10_Ble_Module.BRK, microSD1.GND
  N4: R4.Pin_0, Part1.A+, R3.Pin_0
  5V: FAN.5V, U1.IN+, C1.+, Power_plug1.VCC, Pololu_A3.VMOT, Pololu_A4.VMOT
  GND_2: FAN.GND, U1.IN-, C1.-, Power_plug1.GND, Pololu_A3.GND#14, Pololu_A4.GND#14
  N5: Bauteil4.MOSI, microSD1.MOSI
  N6: Bauteil4.RXLED/SS, microSD1.CS
  N7: Bauteil4.D1/TX, HM10_Ble_Module.RXD
  N8: Bauteil4.D0/RX, HM10_Ble_Module.TXD
  N9: Bauteil4.D2/SDA, Pololu_A3.DIR, Pololu_A4.DIR
  N10: Bauteil4.D3/SCL, Pololu_A3.STEP, Pololu_A4.STEP
  N11: Bauteil4.D5_PWM, J1.pin1, S5.L1
  N12: Bauteil4.D6_PWM/A7, S4.Pin_1, S4.Pin_2, J1.pin2
  N13: Bauteil4.D7, LED1.anode
  N14: Bauteil4.D8_PWM/A8, Pololu_A3.ENABLE, Pololu_A4.ENABLE
  N15: Bauteil4.D12_PWM/A11, SdDetectPin.1
  N16: Bauteil4.SCK, microSD1.SCK
  N17: Bauteil4.MISO, microSD1.MISO
  N18: Bauteil4.VIN, U1.OUT+
  VCC: Bauteil4.5V, Part1.VCC, Pololu_A3.MS1, Pololu_A3.VDD, Pololu_A4.MS1, Pololu_A4.VDD, HM10_Ble_Module.VCC, microSD1.VCC
  N19: Bauteil4.A2, Part1.CK/TX
  N20: Bauteil4.A1, Part1.DO/RX
  N21: R2.Pin_0, Part1.E-, R3.Pin_1
  N22: M2.A, Pololu_A3.2B
  N23: M2.C, Pololu_A3.2A
  N24: M2.B, Pololu_A3.1A
  N25: M2.D, Pololu_A3.1B
  N26: LED1.cathode, R6.Pin_1
  N27: M1.A, Pololu_A4.2B
  N28: M1.C, Pololu_A4.2A
  N29: M1.B, Pololu_A4.1A
  N30: M1.D, Pololu_A4.1B
  N31: Pololu_A3.RESET, Pololu_A3.SLEEP
  N32: Pololu_A4.RESET, Pololu_A4.SLEEP

notes:
  Load cell
  SD Detect Pin

custom parts:
  Fan - Ventilador: Ventilador de 2 pines, se encuentra comunmente en computadoras de escritorio
  Mini-360 DC-DC Buck converter: Mini-360 DC-DC Buck converter. Tiny buck step down voltage converter, input voltage 4.75 to 23V output 1 to 17V adjustable. Available from ebay and the like.
